# Fritzing sketch circuit-diagram (saved by Fritzing 0.9.3b)
breadboards: 1

parts:
  MH-ET_LIVE_ESP32_DEVKIT1 = MH-ET LIVE ESP32 DEVKIT 38 pins
  Part2 = FC-28 Soil Hygrometer Module - Probe
  Part3 = FC-28 Soil Hygrometer Module
  DHT1 = DHT11 Humitidy and Temperature Sensor
  VCC1 = Battery block 9V
  Water_Level_Sensor1 = Water Level Sensor
  Relay_5V1 = Keyes Relay [package=THT]
  WATER_PUMP1 = water pump/motor

nets (from the breadboard view):
  N1: MH-ET_LIVE_ESP32_DEVKIT1.3V3, Relay_5V1.power
  N2: MH-ET_LIVE_ESP32_DEVKIT1.IO33, Part3.AO
  GND: MH-ET_LIVE_ESP32_DEVKIT1.CMD, Part3.GND, DHT1.GND, Water_Level_Sensor1.GND
  VCC: MH-ET_LIVE_ESP32_DEVKIT1.5V, Part3.VCC, DHT1.VDD, VCC1.+, Water_Level_Sensor1.VCC, Relay_5V1.C
  N3: MH-ET_LIVE_ESP32_DEVKIT1.IO5, Water_Level_Sensor1.SIG
  N4: MH-ET_LIVE_ESP32_DEVKIT1.IO17, DHT1.DATA
  N5: MH-ET_LIVE_ESP32_DEVKIT1.IO4, Relay_5V1.signal
  N6: Part2.POS, Part3.POS
  N7: Part2.NEG, Part3.NEG
  N8: VCC1.-, Relay_5V1.ground, WATER_PUMP1.pin_1
  N9: Relay_5V1.NC, WATER_PUMP1.pin_2

custom parts:
  MH-ET LIVE ESP32 DEVKIT 38 pins: http://mh.nodebb.com/topic/2/mh-et-live-esp32-devkit
  FC-28 Soil Hygrometer Module - Probe: The FC-28 is a soil hygrometer module that uses the Texas Instruments LM393 comparator chip to provide an analog measurement of soil humidity.
  FC-28 Soil Hygrometer Module: The FC-28 is a soil hygrometer module that uses the Texas Instruments LM393 comparator chip to provide an analog measurement of soil humidity. The digital output is high when soil moisture is over a certain threshold, as determined by adjusting the potentiometer.
  DHT11 Humitidy and Temperature Sensor: DHT11 Humidity and Temperature Sensor
  Water Level Sensor: A water level sensor. This sensor operates at 3V to 5V. The Sig (signal) pin outputs an analogue signal that is in proportion to the amount of water in contact with the sensor.
  Keyes Relay: The Keyes 5V relay module is suitable for SCM development, home appliance control. It uses a 5V~12V TIL control signal which can control DC / AC signal.
  water pump/motor: WATER PUMP BY ARDUBLOCKTR
